# Fritzing sketch EEG Circuit (saved by Fritzing 0.9.1b)
breadboards: 1

parts:
  IC7 = IC, DIP package, 8 pins [chip_label=AD620]
  R31 = Resistor [tolerance=±5% resistance=560 package=THT]
  IC8 = OP482 - Low Power, High Speed JFET Quad Operational Amplifier [part_number=TL084]
  IC9 = OP482 - Low Power, High Speed JFET Quad Operational Amplifier [part_number=TL084]
  R32 = Resistor [tolerance=±5% resistance=22k package=THT]
  C23 = Ceramic Capacitor [capacitance=220nF package="100 mil [THT, multilayer]"]
  C24 = Electrolytic Capacitor [capacitance=10µF package="100 mil [THT, electrolytic]"]
  R33 = Resistor [tolerance=±5% resistance=220 package=THT]
  R34 = Resistor [tolerance=±5% resistance=12 package=THT]
  C25 = Ceramic Capacitor [capacitance=220nF package="100 mil [THT, multilayer]"]
  C26 = Ceramic Capacitor [capacitance=220nF package="100 mil [THT, multilayer]"]
  C27 = Ceramic Capacitor [capacitance=220nF package="100 mil [THT, multilayer]"]
  R35 = Resistor [tolerance=±5% resistance=220 package=THT]
  R36 = Resistor [tolerance=±5% resistance=180k package=THT]
  R37 = Resistor [tolerance=±5% resistance=180k package=THT]
  R38 = Resistor [tolerance=±5% resistance=180k package=THT]
  C28 = Ceramic Capacitor [capacitance=100nF package="100 mil [THT, multilayer]"]
  C29 = Ceramic Capacitor [capacitance=25nF package="100 mil [THT, multilayer]"]
  C30 = Electrolytic Capacitor [capacitance=1µF package="100 mil [THT, electrolytic]"]
  R39 = Resistor [tolerance=±5% resistance=1M package=THT]
  C31 = Ceramic Capacitor [capacitance=10nF package="100 mil [THT, multilayer]"]
  R40 = Resistor [tolerance=±5% resistance=100 package=THT]
  R41 = Trimmer Potentiometer [maximum_resistance=2kΩ package=THT]
  R42 = Resistor [tolerance=±5% resistance=220 package=THT]
  R43 = Resistor [tolerance=±5% resistance=22k package=THT]
  C32 = Electrolytic Capacitor [capacitance=10µF package="100 mil [THT, electrolytic]"]
  C33 = Ceramic Capacitor [capacitance=220nF package="100 mil [THT, multilayer]"]
  R44 = Resistor [tolerance=±5% resistance=12 package=THT]
  R45 = Resistor [tolerance=±5% resistance=220 package=THT]
  Bat_5 = DC Power [voltage=9 frequency=60]
  Bat_6 = DC Power [voltage=9 frequency=60]
  TRRS1 = Audio Jack (TRRS) 3.5mm [package="RC-5325A [SMD]"]
  C34 = Ceramic Capacitor [capacitance=100nF package="100 mil [THT, multilayer]"]
  R46 = Resistor [tolerance=±5% resistance=1k package=THT]

nets:
  N1: IC7.pin1, R31.Pin_0
  -9V: IC7.pin4, IC8.V-, IC9.V-, Bat_5.V-
  GND: IC7.pin5, IC9.+INB, IC9.+INC, R33.Pin_1, C28.0, R39.Pin_0, R41.leg1, R45.Pin_1, Bat_5.V+, Bat_6.V-, TRRS1.SLEEVE, R46.Pin_1
  N2: IC7.pin6, R32.Pin_0
  9V: IC7.pin7, IC8.V+, IC9.V+, Bat_6.V+
  N3: IC7.pin8, R31.Pin_1
  N4: IC8.OUTA, IC8.-INA, C32.+, R44.Pin_1
  N5: IC8.+INA, C32.-, R45.Pin_0
  N6: IC9.OUTA, IC9.-INA, R34.Pin_1, C25.0
  N7: IC9.+INA, C24.-, R33.Pin_0
  N8: IC9.-INB, C27.1, R35.Pin_1
  N9: IC9.OUTB, C26.1, R35.Pin_0, R37.Pin_0
  N10: IC9.OUTC, R36.Pin_1, C29.1, C30.+
  N11: IC9.-INC, R38.Pin_1, C29.0
  N12: IC9.+IND, C30.-, R39.Pin_1
  N13: IC9.-IND, C31.0, R40.Pin_1, R42.Pin_0
  N14: IC9.OUTD, C31.1, R40.Pin_0, R43.Pin_0
  N15: R32.Pin_1, C23.0
  N16: C23.1, C24.+, R34.Pin_0
  N17: C25.1, C26.0, C27.0
  N18: R36.Pin_0, R37.Pin_1, R38.Pin_0, C28.1
  N19: R41.wiper, R42.Pin_1
  N20: R43.Pin_1, C33.1, C34.0, R46.Pin_0
  N21: C33.0, R44.Pin_0
  N22: TRRS1.RING2, C34.1

notes:
  EEG Circuit 2, By Alexander Pope, 2
